# Fritzing sketch CoG Arduino Setup (saved by Fritzing 0.9.6b)
breadboards: 1

parts:
  Part2 = Arduino Nano (Rev3.0)
  Juror_A = TSOP312.., 314.. [package=THT]
  Seeeduino = Arduino Mega ADK (Rev3)
  Part3 = Arduino Nano (Rev3.0)
  Juror_B = TSOP312.., 314.. [package=THT]
  Part5 = Arduino Nano (Rev3.0)
  Jury_Foreman = TSOP312.., 314.. [package=THT]
  Juror_C = TSOP312.., 314.. [package=THT]
  Part4 = Arduino Nano (Rev3.0)

nets:
  GND: Part2.GND, Juror_A.GND, Seeeduino.GND, Part3.GND, Juror_B.GND, Part5.GND, Jury_Foreman.GND, Juror_C.GND, Part4.GND
  N1: Part2.D3, Juror_A.Data
  N2: Part2.D4, Seeeduino.D2_PWM
  N3: Part2.5V, Juror_A.Vs
  N4: Seeeduino.D3_PWM, Part3.D4
  N5: Seeeduino.D4_PWM, Part4.D4
  N6: Seeeduino.D5_PWM, Part5.D4
  N7: Part3.D3, Juror_B.Data
  N8: Part3.5V, Juror_B.Vs
  N9: Part5.D3, Jury_Foreman.Data
  N10: Part5.5V, Jury_Foreman.Vs
  N11: Juror_C.Vs, Part4.5V
  N12: Juror_C.Data, Part4.D3
